# Fritzing sketch Button and Encoder Connections Schematic (saved by Fritzing 0.9.4)
breadboards: 1

parts:
  Raspberry_Pi2 = Raspberry Pi B+
  Joint_A_Top = SWITCH-MOMENTARY-2 [package=tactile-switch-1101ne]
  Joint_A_Bottom = SWITCH-MOMENTARY-2 [package=tactile-switch-1101ne]
  Joint_B_Bottom = SWITCH-MOMENTARY-2 [package=tactile-switch-1101ne]
  Joint_B_Top = SWITCH-MOMENTARY-2 [package=tactile-switch-1101ne]
  CUI-enc4 = AMT103
  CUI-enc5 = AMT103
  CUI-enc6 = AMT103
  Emergency_Stop = SWITCH-MOMENTARY-2 [package=tactile-switch-1101ne]

nets:
  5V: Raspberry_Pi2.3v3, CUI-enc4.5V, CUI-enc5.5V, CUI-enc6.5V
  N1: Raspberry_Pi2.GPIO17, CUI-enc6.GND
  N2: Raspberry_Pi2.GPIO27, CUI-enc6.X
  N3: Raspberry_Pi2.GPIO22, CUI-enc6.A
  N4: Raspberry_Pi2.GPIO10, CUI-enc5.GND
  N5: Raspberry_Pi2.GPIO9, CUI-enc5.X
  N6: Raspberry_Pi2.GPIO11, CUI-enc5.A
  N7: Raspberry_Pi2.GPIO21, CUI-enc4.A
  N8: Raspberry_Pi2.GPIO20, CUI-enc4.X
  N9: Raspberry_Pi2.GPIO16, CUI-enc4.GND
  N10: Raspberry_Pi2.GPIO7, Joint_B_Bottom.1
  N11: Raspberry_Pi2.GPIO8, Joint_B_Top.1
  N12: Raspberry_Pi2.GPIO25, Emergency_Stop.1
  N13: Raspberry_Pi2.GPIO15, Joint_A_Bottom.1
  N14: Raspberry_Pi2.GPIO14, Joint_A_Top.1
  N15: CUI-enc5.B, CUI-enc6.B
